# Fritzing sketch single-stepper-shield (saved by Fritzing 0.9.3b)
circuit board: 8.46667cm x 5.64444cm
breadboards: 1

parts:
  Pololu_A1 = Pololu A4988 [package=SO16]
  J1 = female pin header, 4 pins [form="♀ (female)"]
  J3 = Screw terminal - 2 pins [package=THT]
  J2 = screw terminal, 4 pins
  Componente1 = Arduino Uno (Rev3)

nets:
  N1: Pololu_A1.ENABLE, J1.pin1, Componente1.D8
  N2: Pololu_A1.MS1, J1.pin2
  N3: Pololu_A1.MS2, J1.pin3
  N4: Pololu_A1.MS3, J1.pin4
  N5: Pololu_A1.RESET, Pololu_A1.SLEEP
  N6: Pololu_A1.STEP, Componente1.D4
  N7: Pololu_A1.DIR, Componente1.D7
  N8: Pololu_A1.GND#8, Componente1.GND
  VDD: Pololu_A1.VDD, Componente1.5V
  N9: Pololu_A1.1B, J2.pin4
  N10: Pololu_A1.1A, J2.pin3
  N11: Pololu_A1.2A, J2.pin2
  N12: Pololu_A1.2B, J2.pin1
  N13: Pololu_A1.GND#14, J3.pin2
  N14: Pololu_A1.VMOT, J3.pin1
